// Logisim project task_1.circ as structural Verilog: 1 circuit, main circuit main
module main (
  input  RESET
);

  wire CLK_out, F1_q, F2_q, F3_q, F4_q, F5_q, F6_q, F7_q, F8_q, xor_1_out, xor_2_out, xor_3_out;

  Clock CLK (.out(CLK_out));
  D_Flip_Flop F1 (.clk(CLK_out), .D(F8_q), .Q(F1_q), .reset(RESET));  // open: Qn, preset, en
  D_Flip_Flop F2 (.clk(CLK_out), .D(F1_q), .Q(F2_q), .reset(RESET));  // open: Qn, preset, en
  D_Flip_Flop F3 (.clk(CLK_out), .D(xor_1_out), .Q(F3_q), .reset(RESET));  // open: Qn, preset, en
  xor xor_1 (xor_1_out, F2_q, F8_q);
  xor xor_2 (xor_2_out, F3_q, F8_q);
  D_Flip_Flop F4 (.clk(CLK_out), .D(xor_2_out), .Q(F4_q), .reset(RESET));  // open: Qn, preset, en
  xor xor_3 (xor_3_out, F4_q, F8_q);
  D_Flip_Flop F5 (.clk(CLK_out), .D(xor_3_out), .Q(F5_q), .reset(RESET));  // open: Qn, preset, en
  D_Flip_Flop F6 (.clk(CLK_out), .D(F5_q), .Q(F6_q), .reset(RESET));  // open: Qn, preset, en
  D_Flip_Flop F7 (.clk(CLK_out), .D(F6_q), .Q(F7_q), .reset(RESET));  // open: Qn, preset, en
  D_Flip_Flop F8 (.clk(CLK_out), .D(F7_q), .Q(F8_q), .reset(RESET));  // open: Qn, preset, en
endmodule
